// Digital circuit ALU-8bit.dig as structural Verilog
module ALU_8bit (
  input  A0,
  input  A1,
  input  A2,
  input  A3,
  input  A4,
  input  A5,
  input  A6,
  input  A7,
  input  B0,
  input  B1,
  input  B2,
  input  B3,
  input  B4,
  input  B5,
  input  B6,
  input  B7,
  input  Soma,
  input  Sub,
  input  Multi,
  input  Div,
  input  NAND,
  input  XOR,
  input  Right,
  input  Left,
  input  Shift,
  input  Clock,
  input  \Div_botão ,
  output Q0,
  output Q1,
  output Q2,
  output Q3,
  output Q4,
  output Q5,
  output Q6,
  output Q7,
  output CO_Soma
);

  wire anda0, anda1, anda2, anda3, anda4, anda5, anda6, anda7, andb0, andb1, andb2, andb3, andb4, andb5,
       andb6, andb7, diva0, diva1, diva2, diva3, diva4, diva5, diva6, diva7, divb0, divb1, divb2, divb3,
       divb4, divb5, divb6, divb7, multia0, multia1, multia2, multia3, multia4, multia5, multia6, multia7,
       multib0, multib1, multib2, multib3, multib4, multib5, multib6, multib7, multiplicador_8bits_1_s8,
       multiplicador_8bits_1_s9, multiplicador_8bits_1_s10, multiplicador_8bits_1_s11,
       multiplicador_8bits_1_s12, multiplicador_8bits_1_s13, multiplicador_8bits_1_s14,
       multiplicador_8bits_1_s15, nand_8bits_1_s0, nand_8bits_1_s1, nand_8bits_1_s2, nand_8bits_1_s3,
       nand_8bits_1_s4, nand_8bits_1_s5, nand_8bits_1_s6, nand_8bits_1_s7, soma_sub_8bits_1_s0,
       soma_sub_8bits_1_s1, soma_sub_8bits_1_s2, soma_sub_8bits_1_s3, soma_sub_8bits_1_s4,
       soma_sub_8bits_1_s5, soma_sub_8bits_1_s6, soma_sub_8bits_1_s7, somaA0, somaA1, somaA2, somaA3, somaA4,
       somaA5, somaA6, somaA7, somaB0, somaB1, somaB2, somaB3, somaB4, somaB5, somaB6, somaB7, xora0, xora1,
       xora2, xora3, xora4, xora5, xora6, xora7, xorb0, xorb1, xorb2, xorb3, xorb4, xorb5, xorb6, xorb7, xs0,
       xs1, xs2, xs3, xs4, xs5, xs6, xs7;
  wire [7:0] s_div, s_multi, s_nand, s_shifter, s_soma, s_sub, s_xor, xor_1_out;

  and and_1 (somaA7, Soma, A7);
  and and_2 (somaB7, Soma, B7);
  and and_3 (somaA6, Soma, A6);
  and and_4 (somaB6, Soma, B6);
  and and_5 (somaA5, Soma, A5);
  and and_6 (somaB5, Soma, B5);
  and and_7 (somaA4, Soma, A4);
  and and_8 (somaB4, Soma, B4);
  and and_9 (somaA3, Soma, A3);
  and and_10 (somaB3, Soma, B3);
  and and_11 (somaA2, Soma, A2);
  and and_12 (somaB2, Soma, B2);
  and and_13 (somaA1, Soma, A1);
  and and_14 (somaB1, Soma, B1);
  and and_15 (somaA0, Soma, A0);
  and and_16 (somaB0, Soma, B0);
  soma_8bits soma_8bits_1 (
    .A7(somaA7), .B7(somaB7), .A6(somaA6), .B6(somaB6), .A5(somaA5), .B5(somaB5), .A4(somaA4), .B4(somaB4),
    .A3(somaA3), .B3(somaB3), .A2(somaA2), .B2(somaB2), .A1(somaA1), .B1(somaB1), .A0(somaA0), .B0(somaB0),
    .S0(s_soma[0]), .S1(s_soma[1]), .S2(s_soma[2]), .S3(s_soma[3]), .S4(s_soma[4]), .S5(s_soma[5]),
    .S6(s_soma[6]), .S7(s_soma[7]), .Co(CO_Soma));
  soma_sub_8bits soma_sub_8bits_1 (
    .SUB(Sub), .B0(B0), .B1(B1), .B2(B2), .B3(B3), .B4(B4), .B5(B5), .B6(B6), .B7(B7), .A0(A0), .A1(A1),
    .A2(A2), .A3(A3), .A4(A4), .A5(A5), .A6(A6), .A7(A7), .S0(soma_sub_8bits_1_s0), .S1(soma_sub_8bits_1_s1),
    .S2(soma_sub_8bits_1_s2), .S3(soma_sub_8bits_1_s3), .S4(soma_sub_8bits_1_s4), .S5(soma_sub_8bits_1_s5),
    .S6(soma_sub_8bits_1_s6), .S7(soma_sub_8bits_1_s7));
  and and_17 (s_sub[0], Sub, soma_sub_8bits_1_s0);
  and and_18 (s_sub[1], Sub, soma_sub_8bits_1_s1);
  and and_19 (s_sub[2], Sub, soma_sub_8bits_1_s2);
  and and_20 (s_sub[3], Sub, soma_sub_8bits_1_s3);
  and and_21 (s_sub[4], Sub, soma_sub_8bits_1_s4);
  and and_22 (s_sub[5], Sub, soma_sub_8bits_1_s5);
  and and_23 (s_sub[6], Sub, soma_sub_8bits_1_s6);
  and and_24 (s_sub[7], Sub, soma_sub_8bits_1_s7);
  and and_25 (multia0, Multi, A0);
  and and_26 (multia1, Multi, A1);
  and and_27 (multia2, Multi, A2);
  and and_28 (multia3, Multi, A3);
  and and_29 (multia4, Multi, A4);
  and and_30 (multia5, Multi, A5);
  and and_31 (multia6, Multi, A6);
  and and_32 (multia7, Multi, A7);
  and and_33 (multib0, Multi, B0);
  and and_34 (multib1, Multi, B1);
  and and_35 (multib2, Multi, B2);
  and and_36 (multib3, Multi, B3);
  and and_37 (multib4, Multi, B4);
  and and_38 (multib5, Multi, B5);
  and and_39 (multib6, Multi, B6);
  and and_40 (multib7, Multi, B7);
  multiplicador_8bits multiplicador_8bits_1 (
    .A0(multia0), .A1(multia1), .A2(multia2), .A3(multia3), .A4(multia4), .A5(multia5), .A6(multia6),
    .A7(multia7), .B0(multib0), .B1(multib1), .B2(multib2), .B3(multib3), .B4(multib4), .B5(multib5),
    .B6(multib6), .B7(multib7), .S0(s_multi[0]), .S1(s_multi[1]), .S2(s_multi[2]), .S3(s_multi[3]),
    .S4(s_multi[4]), .S5(s_multi[5]), .S6(s_multi[6]), .S7(s_multi[7]), .S8(multiplicador_8bits_1_s8),
    .S9(multiplicador_8bits_1_s9), .S10(multiplicador_8bits_1_s10), .S11(multiplicador_8bits_1_s11),
    .S12(multiplicador_8bits_1_s12), .S13(multiplicador_8bits_1_s13), .S14(multiplicador_8bits_1_s14),
    .S15(multiplicador_8bits_1_s15));
  and and_41 (diva0, Div, A0);
  and and_42 (diva1, Div, A1);
  and and_43 (diva2, Div, A2);
  and and_44 (diva3, Div, A3);
  and and_45 (diva4, Div, A4);
  and and_46 (diva5, Div, A5);
  and and_47 (diva6, Div, A6);
  and and_48 (diva7, Div, A7);
  and and_49 (divb0, Div, B0);
  and and_50 (divb1, Div, B1);
  and and_51 (divb2, Div, B2);
  and and_52 (divb3, Div, B3);
  and and_53 (divb4, Div, B4);
  and and_54 (divb5, Div, B5);
  and and_55 (divb6, Div, B6);
  and and_56 (divb7, Div, B7);
  divisor_8bits divisor_8bits_1 (
    .A0(diva0), .B0(divb0), .A1(diva1), .B1(divb1), .A2(diva2), .B2(divb2), .A3(diva3), .B3(divb3),
    .A4(diva4), .B4(divb4), .A5(diva5), .B5(divb5), .A6(diva6), .B6(divb6), .A7(diva7), .B7(divb7),
    .Clock(Clock), .Div(\Div_botão ), .S0(s_div[0]), .S1(s_div[1]), .S2(s_div[2]), .S3(s_div[3]),
    .S4(s_div[4]), .S5(s_div[5]), .S6(s_div[6]), .S7(s_div[7]));
  and and_57 (anda0, NAND, A0);
  and and_58 (anda1, NAND, A1);
  and and_59 (anda2, NAND, A2);
  and and_60 (anda3, NAND, A3);
  and and_61 (anda4, NAND, A4);
  and and_62 (anda5, NAND, A5);
  and and_63 (anda6, NAND, A6);
  and and_64 (anda7, NAND, A7);
  and and_65 (andb0, NAND, B0);
  and and_66 (andb1, NAND, B1);
  and and_67 (andb2, NAND, B2);
  and and_68 (andb3, NAND, B3);
  and and_69 (andb4, NAND, B4);
  and and_70 (andb5, NAND, B5);
  and and_71 (andb6, NAND, B6);
  and and_72 (andb7, NAND, B7);
  NAND_8bits nand_8bits_1 (
    .A0(anda0), .A1(anda1), .A2(anda2), .A3(anda3), .A4(anda4), .A5(anda5), .A6(anda6), .A7(anda7),
    .B0(andb0), .B1(andb1), .B2(andb2), .B3(andb3), .B4(andb4), .B5(andb5), .B6(andb6), .B7(andb7),
    .S0(nand_8bits_1_s0), .S1(nand_8bits_1_s1), .S2(nand_8bits_1_s2), .S3(nand_8bits_1_s3),
    .S4(nand_8bits_1_s4), .S5(nand_8bits_1_s5), .S6(nand_8bits_1_s6), .S7(nand_8bits_1_s7));
  and and_73 (s_nand[0], NAND, nand_8bits_1_s0);
  and and_74 (s_nand[1], NAND, nand_8bits_1_s1);
  and and_75 (s_nand[2], NAND, nand_8bits_1_s2);
  and and_76 (s_nand[3], NAND, nand_8bits_1_s3);
  and and_77 (s_nand[4], NAND, nand_8bits_1_s4);
  and and_78 (s_nand[5], NAND, nand_8bits_1_s5);
  and and_79 (s_nand[6], NAND, nand_8bits_1_s6);
  and and_80 (s_nand[7], NAND, nand_8bits_1_s7);
  and and_81 (xora0, XOR, A0);
  and and_82 (xora1, XOR, A1);
  and and_83 (xora2, XOR, A2);
  and and_84 (xora3, XOR, A3);
  and and_85 (xora4, XOR, A4);
  and and_86 (xora5, XOR, A5);
  and and_87 (xora6, XOR, A6);
  and and_88 (xora7, XOR, A7);
  and and_89 (xorb0, XOR, B0);
  and and_90 (xorb1, XOR, B1);
  and and_91 (xorb2, XOR, B2);
  and and_92 (xorb3, XOR, B3);
  and and_93 (xorb4, XOR, B4);
  and and_94 (xorb5, XOR, B5);
  and and_95 (xorb6, XOR, B6);
  and and_96 (xorb7, XOR, B7);
  XOR_8bits xor_8bits_1 (
    .A0(xora0), .A1(xora1), .A2(xora2), .A3(xora3), .A4(xora4), .A5(xora5), .A6(xora6), .A7(xora7),
    .B0(xorb0), .B1(xorb1), .B2(xorb2), .B3(xorb3), .B4(xorb4), .B5(xorb5), .B6(xorb6), .B7(xorb7),
    .S0(s_xor[0]), .S1(s_xor[1]), .S2(s_xor[2]), .S3(s_xor[3]), .S4(s_xor[4]), .S5(s_xor[5]), .S6(s_xor[6]),
    .S7(s_xor[7]));
  XOR_8bits xor_8bits_2 (
    .A0(A0), .A1(A1), .A2(A2), .A3(A3), .A4(A4), .A5(A5), .A6(A6), .A7(A7), .B0(B0), .B1(B1), .B2(B2),
    .B3(B3), .B4(B4), .B5(B5), .B6(B6), .B7(B7), .S0(xs0), .S1(xs1), .S2(xs2), .S3(xs3), .S4(xs4), .S5(xs5),
    .S6(xs6), .S7(xs7));
  shitfer_completo_8bits shitfer_completo_8bits_1 (
    .S7(s_shifter[7]), .S6(s_shifter[6]), .S5(s_shifter[5]), .S4(s_shifter[4]), .S3(s_shifter[3]),
    .S2(s_shifter[2]), .S1(s_shifter[1]), .S0(s_shifter[0]), .right(Right), .left(Left), .A7(xs7), .A6(xs6),
    .A5(xs5), .A4(xs4), .A3(xs3), .A2(xs2), .A1(xs1), .A0(xs0), .shift(Shift));
  assign xor_1_out = s_soma ^ s_sub ^ s_multi ^ s_div ^ s_nand ^ s_xor ^ s_shifter;  // XOr xor_1, 8 bits wide
  registrador_8bits registrador_8bits_1 (
    .D7(xor_1_out[7]), .D6(xor_1_out[6]), .D5(xor_1_out[5]), .D4(xor_1_out[4]), .D3(xor_1_out[3]),
    .D2(xor_1_out[2]), .D1(xor_1_out[1]), .D0(xor_1_out[0]), .Clock(Clock), .Q7(Q7), .Q6(Q6), .Q5(Q5),
    .Q4(Q4), .Q3(Q3), .Q2(Q2), .Q1(Q1), .Q0(Q0));
endmodule
