// Digital circuit ALU-visual.dig as structural Verilog
module ALU_visual (
  input  A0,
  input  A1,
  input  A2,
  input  A3,
  input  A4,
  input  A5,
  input  A6,
  input  A7,
  input  B0,
  input  B1,
  input  B2,
  input  B3,
  input  B4,
  input  B5,
  input  B6,
  input  B7,
  input  Soma,
  input  Sub,
  input  Multi,
  input  Div,
  input  Nand,
  input  Xor,
  input  Right,
  input  Left,
  input  Clock
);

  wire alu_8bit_1_co_soma, div_botao, shift;
  wire [3:0] alu_8bit_1_q0, alu_8bit_1_q4;

  Button u_Shift (.out(shift));
  Button u_Div_botao (.out(div_botao));
  ALU_8bit alu_8bit_1 (
    .A0(A0), .A1(A1), .A2(A2), .A3(A3), .A4(A4), .A5(A5), .A6(A6), .A7(A7), .B0(B0), .B1(B1), .B2(B2),
    .B3(B3), .B4(B4), .B5(B5), .B6(B6), .B7(B7), .Soma(Soma), .Sub(Sub), .Multi(Multi), .Div(Div),
    .NAND(Nand), .XOR(Xor), .Right(Right), .Left(Left), .Shift(shift), .Clock(Clock),
    .\Div_botão (div_botao), .Q0(alu_8bit_1_q0[0]), .Q1(alu_8bit_1_q0[1]), .Q2(alu_8bit_1_q0[2]),
    .Q3(alu_8bit_1_q0[3]), .Q4(alu_8bit_1_q4[0]), .Q5(alu_8bit_1_q4[1]), .Q6(alu_8bit_1_q4[2]),
    .Q7(alu_8bit_1_q4[3]), .CO_Soma(alu_8bit_1_co_soma));
  Seven_Seg_Hex seven_seg_hex_1 (.d(alu_8bit_1_q4), .dp(1'b0));
  Seven_Seg_Hex seven_seg_hex_2 (.d(alu_8bit_1_q0), .dp(alu_8bit_1_co_soma));
endmodule
