// Digital circuit CPU-8BITS.dig as structural Verilog
module CPU_8BITS (
  output [7:0] Ac,
  output [7:0] Mq
);

  wire clk, q, q_t;
  wire [7:0] pc_1_addr;
  wire [10:0] register_1_q, rom_1_d;

  Button u_Clk (.out(clk));
  PC pc_1 (.Clk(clk), .En(q), .Addr(pc_1_addr));
  D_FF d_ff_1 (.D(q_t), .C(clk), .Q(q), .nQ(q_t));
  ROM #(.AddrBits(8), .Bits(11)) rom_1 (.A(pc_1_addr), .sel(q_t), .D(rom_1_d));
  Register #(.Bits(11)) register_1 (.D(rom_1_d), .C(clk), .en(q_t), .Q(register_1_q));
  ALU_visual alu_visual_1 (.N(register_1_q[7:0]), .En(q), .Clk(clk), .Op(register_1_q[10:8]), .Ac(Ac), .Mq(Mq));

  // Notes on the sheet:
  //   0 - adiciona 1
  //   1 - soma 3
  //   2 - divide 8 por B
  //   3 - multiplica por 2
  //   contents of rom_1 (hex, n*v repeats v):
  //   3,101,20a,305,404,5f9,600,700
endmodule
